# Fritzing sketch sketch (saved by Fritzing 0.9.9b)
circuit board: 6.3cm x 6.3cm
breadboards: 2

parts:
  IC1 = ULN2803A [package=THT]
  U1 = LuaNode32 / ESP32 [part_number=ESP32S-PIN30]
  JACK1 = 2.1mm Barrel Jack with Terminal Block
  L1 = Solenoid

nets:
  N1: IC1.In_1, U1.D13
  N2: IC1.0V, U1.GND, JACK1.NEG, L1.pin1
  N3: IC1.COM_-_Common, JACK1.POS
  N4: IC1.Out_1, L1.pin2

notes:
  12 V DC input
  solenoid or any other component

custom parts:
  LuaNode32 / ESP32: New Image for LuaNode32 DOIT ESP32 DEVKIT V1. Base parts from LuaNode32 / ESP32 ESP32 based LuaNode32 by G.Noorlander DOIT Esp32 DevKit v1 (30 pins long, 11 pins width) by Werner Rothschopf (modified by vanepp Dec 2018)
